# Fritzing sketch escape_room_arduino (saved by Fritzing 0.9.3b)
breadboards: 1

parts:
  Part1 = Arduino Uno (Rev3)
  U1 = 7-SEGMENT-4DIGIT [package=7-segment-4digit]
  LED1 = smd LED [color="Green (565nm)" package="0805 [SMD]"]
  LED2 = smd LED [color="Green (565nm)" package="0805 [SMD]"]  # not connected
  U4 = 74HC595 [package="DIP16 [THT]"]
  J1 = Basic Servo
  Matrix_keypad1 = KEYPAD 4x4
  J2 = Piezo Speaker
  LED3 = smd LED [color="Red (660nm)" package="0805 [SMD]"]
  R1 = Resistor [tolerance=±5% resistance=220 package="0603 [SMD]"]
  U5 = LCD-16X2 [package=lcd-16x2_nosilk]

nets:
  N1: Part1.A0, Matrix_keypad1.col4
  N2: Part1.A1, Matrix_keypad1.row2
  N3: Part1.A2, Matrix_keypad1.col2
  N4: Part1.A3, Matrix_keypad1.col1
  N5: Part1.D8, U1.16
  N6: Part1.D9_PWM, LED1.cathode
  N7: Part1.D10_PWM/SS, J1.pulse
  N8: Part1.D11_PWM/MOSI, LED3.cathode
  N9: Part1.D12/MISO, J2.pin2
  GND: Part1.GND, J1.gnd, J2.pin1, R1.Pin_1, U5.A
  N10: Part1.A4/SDA, U5.DB7
  N11: Part1.A5/SCL, U5.DB6
  N12: Part1.D2, U4.SH_CP
  N13: Part1.D3_PWM, U4.ST_CP
  N14: Part1.D4, U4.DS
  N15: Part1.D7, U1.13
  5V: Part1.5V, U4.MR, J1.vcc, U5.K
  N16: LED1.anode, LED3.anode, R1.Pin_0

custom parts:
  KEYPAD 4x4: Matrix keypad 16 buttons, 4 rows x 4 columns
