# Fritzing sketch escape_room_esp32 (saved by Fritzing 0.9.3b)

parts:
  MH-ET_LIVE_ESP32_DEVKIT2 = MH-ET LIVE ESP32 DEVKIT 38 pins
  Part3 = RFID-RC522-v2
  BAT1 = BC9VPC [package=bc9vpc]

nets:
  3V3: MH-ET_LIVE_ESP32_DEVKIT2.3V3, Part3.3.3V
  N1: MH-ET_LIVE_ESP32_DEVKIT2.GND#58, BAT1.V-
  N2: MH-ET_LIVE_ESP32_DEVKIT2.5V, BAT1.V+
  N3: MH-ET_LIVE_ESP32_DEVKIT2.GND#64, Part3.GND
  N4: MH-ET_LIVE_ESP32_DEVKIT2.IO23, Part3.MOSI
  N5: MH-ET_LIVE_ESP32_DEVKIT2.IO22, Part3.RST
  N6: MH-ET_LIVE_ESP32_DEVKIT2.IO21, Part3.SDA
  N7: MH-ET_LIVE_ESP32_DEVKIT2.IO19, Part3.MISO
  N8: MH-ET_LIVE_ESP32_DEVKIT2.IO18, Part3.SCK

custom parts:
  MH-ET LIVE ESP32 DEVKIT 38 pins: http://mh.nodebb.com/topic/2/mh-et-live-esp32-devkit
  RFID-RC522-v2: A simple China made RFID-RC522 Reader; do check the pin labels, as this is a MFRC522 based clone.
